// Logisim project D8421_4.circ as structural Verilog: 1 circuit, main circuit D8421_4_e3091947
module D8421_4_e3091947 (
);

  wire and_1_out, and_2_out, and_3_out, and_4_out, and_5_out, and_6_out, and_7_out, and_8_out, and_9_out,
       and_10_out, and_11_out, and_12_out, and_13_out, and_14_out, dipswitch_1_sw1, dipswitch_1_sw2,
       dipswitch_1_sw3, dipswitch_1_sw4, not_1_out, not_2_out, not_3_out, not_4_out, or_1_out, or_2_out,
       or_3_out, or_4_out, or_5_out;

  DipSwitch #(.number(4)) dipswitch_1 (
    .sw1(dipswitch_1_sw1), .sw2(dipswitch_1_sw2), .sw3(dipswitch_1_sw3), .sw4(dipswitch_1_sw4));
  and and_1 (and_1_out, dipswitch_1_sw1, not_3_out);
  not not_1 (not_1_out, dipswitch_1_sw3);
  not not_2 (not_2_out, dipswitch_1_sw1);
  not not_3 (not_3_out, dipswitch_1_sw2);
  not not_4 (not_4_out, dipswitch_1_sw3);
  and and_2 (and_2_out, and_1_out, not_1_out);
  and and_3 (and_3_out, not_2_out, dipswitch_1_sw2);
  and and_4 (and_4_out, not_2_out, not_3_out);
  and and_5 (and_5_out, not_3_out, dipswitch_1_sw1);
  and and_6 (and_6_out, not_2_out, dipswitch_1_sw3);
  and and_7 (and_7_out, not_2_out, dipswitch_1_sw3);
  and and_8 (and_8_out, dipswitch_1_sw4, not_2_out);
  and and_9 (and_9_out, not_2_out, dipswitch_1_sw4);
  and and_10 (and_10_out, dipswitch_1_sw1, not_3_out);
  and and_11 (and_11_out, not_4_out, dipswitch_1_sw4);
  or or_1 (or_1_out, and_2_out, and_3_out);
  and and_12 (and_12_out, and_7_out, dipswitch_1_sw4);
  and and_13 (and_13_out, and_9_out, dipswitch_1_sw3);
  and and_14 (and_14_out, and_10_out, and_11_out);
  or or_2 (or_2_out, and_4_out, and_5_out);
  or or_3 (or_3_out, and_6_out, and_12_out);
  or or_4 (or_4_out, and_8_out, and_13_out);
  LED Y1 (.in(or_1_out));
  LED Y2 (.in(or_2_out));
  LED Y3 (.in(or_3_out));
  LED Y4 (.in(or_5_out));
  or or_5 (or_5_out, or_4_out, and_14_out);
endmodule
