// Logisim project ODS_3.circ as structural Verilog: 1 circuit, main circuit main
module main (
);

  wire A_sw1, A_sw2, A_sw3, and_1_out, and_2_out, and_3_out, and_4_out, and_5_out, and_6_out, and_7_out,
       and_8_out, and_9_out, and_10_out, and_11_out, and_12_out, and_13_out, and_14_out, and_15_out,
       and_16_out, and_17_out, dipswitch_1_sw1, dipswitch_1_sw2, dipswitch_1_sw3, not_1_out, not_2_out,
       not_3_out, not_4_out, not_5_out, not_6_out, not_7_out, not_8_out, or_1_out, or_2_out, or_3_out,
       or_4_out, or_5_out, or_6_out, xor_1_out, xor_2_out;

  DipSwitch #(.number(3)) A (.sw1(A_sw1), .sw2(A_sw2), .sw3(A_sw3));
  not not_1 (not_1_out, A_sw1);
  not not_2 (not_2_out, A_sw3);
  not not_3 (not_3_out, A_sw2);
  not not_4 (not_4_out, A_sw2);
  not not_5 (not_5_out, A_sw3);
  not not_6 (not_6_out, A_sw1);
  not not_7 (not_7_out, A_sw2);
  not not_8 (not_8_out, A_sw2);
  and and_1 (and_1_out, not_1_out, A_sw2);
  and and_2 (and_2_out, A_sw2, not_2_out);
  and and_3 (and_3_out, A_sw1, not_3_out);
  and and_4 (and_4_out, not_4_out, not_5_out);
  and and_5 (and_5_out, not_6_out, not_7_out);
  and and_6 (and_6_out, not_8_out, A_sw3);
  and and_7 (and_7_out, A_sw1, A_sw2);
  and and_8 (and_8_out, A_sw2, A_sw3);
  and and_9 (and_9_out, and_1_out, and_2_out);
  and and_10 (and_10_out, and_3_out, and_4_out);
  and and_11 (and_11_out, and_5_out, and_6_out);
  and and_12 (and_12_out, and_7_out, and_8_out);
  or or_1 (or_1_out, and_9_out, and_10_out);
  or or_2 (or_2_out, and_11_out, and_12_out);
  and and_13 (and_13_out, A_sw1, A_sw2);
  and and_14 (and_14_out, A_sw1, A_sw3);
  and and_15 (and_15_out, A_sw2, A_sw3);
  or or_3 (or_3_out, or_1_out, or_2_out);
  or or_4 (or_4_out, and_13_out, and_14_out);
  or or_5 (or_5_out, or_4_out, and_15_out);
  DipSwitch #(.number(3)) dipswitch_1 (.sw1(dipswitch_1_sw1), .sw2(dipswitch_1_sw2), .sw3(dipswitch_1_sw3));
  LED Res (.in(or_3_out));
  LED Trun (.in(or_5_out));
  xor xor_1 (xor_1_out, dipswitch_1_sw1, dipswitch_1_sw2);
  and and_16 (and_16_out, xor_1_out, dipswitch_1_sw3);
  and and_17 (and_17_out, dipswitch_1_sw1, dipswitch_1_sw2);
  xor xor_2 (xor_2_out, xor_1_out, dipswitch_1_sw3);
  or or_6 (or_6_out, and_16_out, and_17_out);
  LED Res2 (.in(xor_2_out));
  LED Trun2 (.in(or_6_out));
endmodule
