// Logisim project lr5.circ as structural Verilog: 2 circuits, main circuit main
module main (
  input  V
);

  wire and_1_out, and_2_out, and_3_out, button_1_out, T1_q, T1_qn, T2_q, T2_qn, T3_q, T3_qn, T4_q;

  Button button_1 (.out(button_1_out));
  and and_1 (and_1_out, T1_qn, V);
  and and_2 (and_2_out, T2_qn, T1_qn, V);
  and and_3 (and_3_out, T3_qn, T2_qn, T1_qn, V);
  T_Flip_Flop T1 (.T(V), .clk(button_1_out), .Q(T1_q), .Qn(T1_qn));  // open: reset, preset
  T_Flip_Flop T2 (.T(and_1_out), .clk(button_1_out), .Q(T2_q), .Qn(T2_qn));  // open: reset, preset
  T_Flip_Flop T3 (.T(and_2_out), .clk(button_1_out), .Q(T3_q), .Qn(T3_qn));  // open: reset, preset
  T_Flip_Flop T4 (.T(and_3_out), .clk(button_1_out), .Q(T4_q));  // open: Qn, reset, preset
  // Probe on T1_q
  // Probe on T2_q
  // Probe on T3_q
  // Probe on T4_q
endmodule

module dop (
  input  in_1,
  input  in_2,
  input  in_3,
  input  in_4,
  input  in_5,
  input  in_6,
  input  in_7,
  input  in_8,
  input  in_9,
  input  in_10,
  output out_11,
  output out_12,
  output out_13,
  output out_14
);

  wire d_ff_1_q, d_ff_1_qn, t_ff_1_q, t_ff_1_qn;

  D_Flip_Flop d_ff_1 (.D(in_1), .clk(in_2), .Q(d_ff_1_q), .Qn(d_ff_1_qn));  // open: preset, reset
  S_R_Flip_Flop s_r_ff_1 (.S(in_3), .R(in_5), .clk(in_7), .Q(out_11), .Qn(out_12));  // open: reset, preset
  J_K_Flip_Flop j_k_ff_1 (.J(in_8), .K(in_9), .clk(in_10), .Q(out_13), .Qn(out_14));  // open: preset, reset
  // Probe on d_ff_1_q
  // Probe on d_ff_1_qn
  T_Flip_Flop t_ff_1 (.T(in_4), .clk(in_6), .Q(t_ff_1_q), .Qn(t_ff_1_qn));  // open: reset, preset
  // Probe on t_ff_1_q
  // Probe on t_ff_1_qn
endmodule
